// Logisim project test.circ as structural Verilog: 1 circuit, main circuit main
module main (
  input  RST,
  input  CLK,
  input  LOAD,
  input  [12:0] ADDR,
  input  [15:0] IN,
  output [15:0] OUT
);

  // HACK_Video_Display hack_video_display_1: pin names not known; wires that end beside it: RST, CLK, LOAD, ADDR, IN, OUT
endmodule
